// Logisim project l01.circ as structural Verilog: 3 circuits, main circuit main
module main (
  input  A,
  input  B,
  input  V1,
  output S,
  output VAI1
);

  wire and_1_out, and_2_out, or_1_out, xor_1_out;

  and and_1 (and_1_out, B, V1);
  xor xor_1 (xor_1_out, B, A);
  or or_1 (or_1_out, V1, B);
  and and_2 (and_2_out, or_1_out, A);
  xor xor_2 (S, V1, xor_1_out);
  or or_2 (VAI1, and_2_out, and_1_out);
endmodule

module _2 (
  input  [3:0] B,
  input  [3:0] A,
  output out_3,
  output [3:0] out_4
);

  wire main_2_vai1, main_3_vai1, main_4_vai1;

  main main_1 (.S(out_4[3]), .VAI1(out_3), .A(A[3]), .B(B[3]), .V1(main_3_vai1));
  main main_2 (.S(out_4[1]), .VAI1(main_2_vai1), .A(A[1]), .B(B[1]), .V1(main_4_vai1));
  main main_3 (.S(out_4[2]), .VAI1(main_3_vai1), .A(A[2]), .B(B[2]), .V1(main_2_vai1));
  main main_4 (.S(out_4[0]), .VAI1(main_4_vai1), .A(A[0]), .B(B[0]), .V1(1'b0));

  // Notes on the sheet:
  //   overflow
endmodule

module \final  (
  input  [3:0] in_1,
  input  [3:0] in_2,
  output out_3,
  output [3:0] out_4
);

  // Probe on in_1
  _2 u_2_1 (.A(in_1), .B(in_2), .out_4(out_4), .out_3(out_3));
  // Probe on out_4
  // Probe on in_2
endmodule
